// Logisim project lab 6 mux problem 1.circ as structural Verilog: 1 circuit, main circuit main
module main (
  input  Z,
  input  Y,
  input  X,
  input  W,
  output out_5
);

  Multiplexer #(.select(4), .enable("false")) multiplexer_1 (
    .in0(1'b0), .in1(1'b1), .in2(1'b1), .in3(1'b0), .in4(1'b1), .in5(1'b0), .in6(1'b1), .in7(1'b1),
    .in8(1'b0), .in9(1'b1), .in10(1'b0), .in11(1'b0), .in12(1'b0), .in13(1'b1), .in14(1'b1), .in15(1'b0),
    .out(out_5), .sel({W, X, Y, Z}));
endmodule
