// Logisim project lab 6 mux problem 2.circ as structural Verilog: 1 circuit, main circuit main
module main (
  input  Z,
  input  Y,
  input  X,
  input  W,
  input  U,
  output out_6
);

  Multiplexer #(.select(5), .enable("false")) multiplexer_1 (
    .in0(1'b1), .in1(1'b1), .in2(1'b0), .in3(1'b1), .in4(1'b1), .in5(1'b0), .in6(1'b1), .in7(1'b0),
    .in8(1'b1), .in9(1'b1), .in10(1'b1), .in11(1'b0), .in12(1'b1), .in13(1'b0), .in14(1'b0), .in15(1'b1),
    .in16(1'b1), .in17(1'b0), .in18(1'b1), .in19(1'b1), .in20(1'b1), .in21(1'b1), .in22(1'b0), .in23(1'b0),
    .in24(1'b1), .in25(1'b1), .in26(1'b1), .in27(1'b0), .in28(1'b0), .in29(1'b0), .in30(1'b0), .in31(1'b0),
    .out(out_6), .sel({U, W, X, Y, Z}));
endmodule
