// Logisim project majority multiplex.circ as structural Verilog: 1 circuit, main circuit main
module main (
  input  Z,
  input  Y,
  input  X,
  output Majority
);

  Multiplexer #(.select(2), .enable("false")) multiplexer_1 (
    .in0(1'b0), .in1(Z), .in2(Z), .in3(1'b1), .out(Majority), .sel({X, Y}));

  // Notes on the sheet:
  //   Majority Circuit using 4-1Mux
endmodule
